# Fritzing sketch Pak Iman-monitoring ph meter (saved by Fritzing 0.9.3b)

parts:
  U1 = ESP32-38PinWide [part_number=ESP32-38PinWide]
  Part1 = MicroSD Card Module
  S1 = PH meter [package=THT]
  U4 = LM2596 step down module
  A1 = tds-sensor-meter-v1.0_1
  hc-sr1 = hc-sr04
  RY1 = SSR-40VA

nets:
  N1: U1.GPIO34, A1.pin1
  N2: U1.GPIO35, S1.pin1
  GND: U1.GPIO11, Part1.GND, S1.pin3, U4.OUT-, A1.pin3, hc-sr1.GND, RY1.Pin_4
  VCC: U1.VIN, Part1.VCC, S1.pin2, U4.OUT+, A1.pin2, hc-sr1.VCC
  N3: U1.GPIO5, Part1.CS
  N4: U1.GPIO18, Part1.SCK
  N5: U1.GPIO19, Part1.MISO
  N6: U1.GPIO21, hc-sr1.Echo
  N7: U1.GPIO3, hc-sr1.Trig
  N8: U1.GPIO1, RY1.Pin_3
  N9: U1.GPIO23, Part1.MOSI

notes:
  PH Modul Sensor
  TDS Modul Sensor
  Step Down Modul
  MicroSD
  Ultrasonic
  Relay Motor

custom parts:
  ESP32-38PinWide: Generic 38-Pin ESP32 with wide format (only access to one side of pins on a breadboard) based on Stephen Lilley's HiLetgo ESP-WROOM-32 ESP32 ESP-32S Development Board.
  LM2596 step down module: LM2596 DC-DC step down power supply module 3 A.
  : TDS Meter V1.0 Development Board Water Meter Filter Measuring Water Sensor Module.
  SSR-40VA: SSR-40VA solid state relay.
