# Fritzing sketch aws esp32 (saved by Fritzing 0.9.3b)

parts:
  U1 = ESP32-38PinWide [part_number=ESP32-38PinWide]
  LCD2004-I2C1 = LCD2004-I2C
  Part1 = MicroSD Card Module
  e-radionica_com1 = LM393 LDR breakout [part_number=100027]
  U2 = LM2596 step down module
  M1 = BME280
  A1 = tipping bucket rain-gauge
  J1 = Power Jack [package=power_jack_combo]
  M2 = Adafruit Anemometer [package=THT]

nets:
  N1: U1.GPIO39, e-radionica_com1.AO
  N2: U1.GPIO34, A1.Pin_1
  N3: U1.GPIO35, M2.pin3
  GND: U1.GPIO11, Part1.GND, e-radionica_com1.GND, U2.IN-, U2.OUT-, M1.GND, A1.Pin_2, J1.GNDBREAK, M2.pin2
  VCC: U1.VIN, Part1.VCC, e-radionica_com1.VCC, U2.OUT+, A1.Pin_3, M2.pin1
  N4: U1.GPIO6, Part1.SCK
  N5: U1.GPIO7, Part1.MOSI
  N6: U1.GPIO8, Part1.MISO
  N7: U1.GPIO15, Part1.CS
  N8: U1.GPIO21, LCD2004-I2C1.SDA, M1.SDA
  N9: U1.GPIO22, LCD2004-I2C1.SCL, M1.SCL
  VCC_2: LCD2004-I2C1.VCC, M1.VIN
  N10: U2.IN+, J1.PWR

notes:
  Tipping Bucket Sensor
  Modul MicroSD
  LM2596
  BME380
  Wind Sensor Anemometer
  LDR Modul
  LCD 20*4

custom parts:
  ESP32-38PinWide: Generic 38-Pin ESP32 with wide format (only access to one side of pins on a breadboard) based on Stephen Lilley's HiLetgo ESP-WROOM-32 ESP32 ESP-32S Development Board.
  LCD2004-I2C: A standard character display with 4x20 characters. Comes in many colors with LCM2004 IIC attached.
  LM2596 step down module: LM2596 DC-DC step down power supply module 3 A.
  BME280: Temperature Humidity Barometric presure Sensor
  tipping bucket rain-gauge: This high quality weather proof sensor measures rainfall using a self emptying tipping bucket.
  Adafruit Anemometer: Adafruit Anemometer Wind Speed Sensor w/Analog Voltage Output.
